// Logisim project Flip-Flop-JK.circ as structural Verilog: 1 circuit, main circuit main
module main (
  input  J,
  input  K,
  output Q,
  output nQ
);

  wire clock_1_out, nand_1_out, nand_2_out;

  Clock clock_1 (.out(clock_1_out));
  nand nand_1 (nand_1_out, Q, J, clock_1_out);
  nand nand_2 (nand_2_out, clock_1_out, K, nQ);
  nor nor_1 (Q, nand_1_out, nQ);
  nor nor_2 (nQ, Q, nand_2_out);

  // Notes on the sheet:
  //   Clock
endmodule
